// Logisim project cpu.circ as structural Verilog
module ULA (
  input  [7:0] A,
  input  [7:0] B,
  input  [1:0] S,
  output [7:0] out_4,
  output out_5
);

  wire [7:0] adder_1_out, and_1_out, multiplier_1_out, or_1_out;

  Adder adder_1 (.a(A), .b(B), .out(adder_1_out));  // open: cin, cout
  Multiplier multiplier_1 (.a(A), .b(B), .out(multiplier_1_out));  // open: cin, cout
  assign and_1_out = A & B;  // AND_Gate and_1, 8 bits wide
  assign or_1_out = A | B;  // OR_Gate or_1, 8 bits wide
  Comparator #(.mode("unsigned")) comparator_1 (.a(A), .b(B), .gt(out_5));  // open: eq, lt
  Multiplexer #(.select(2), .width(8)) multiplexer_1 (
    .in0(adder_1_out), .in1(multiplier_1_out), .in2(and_1_out), .in3(or_1_out), .out(out_4), .sel(S));  // open: en
endmodule

module REGS (
  input  [1:0] adda,
  input  [1:0] addb,
  input  [7:0] \input ,
  input  clk,
  input  reset,
  input  en,
  output [7:0] outa,
  output [7:0] outb
);

  wire en0, en1, en2, en3;
  wire [7:0] q0, q1, q2, q3;

  Register register_1 (.D(\input ), .en(en0), .Q(q0), .clk(clk), .clr(reset));
  Register register_2 (.D(\input ), .en(en2), .Q(q2), .clk(clk), .clr(reset));
  Multiplexer #(.select(2), .width(8)) multiplexer_1 (
    .in0(q0), .in1(q1), .in2(q2), .in3(q3), .out(outb), .sel(addb));  // open: en
  Register register_3 (.D(\input ), .en(en1), .Q(q1), .clk(clk), .clr(reset));
  Register register_4 (.D(\input ), .en(en3), .Q(q3), .clk(clk), .clr(reset));
  Multiplexer #(.select(2), .width(8)) multiplexer_2 (
    .in0(q0), .in1(q1), .in2(q2), .in3(q3), .out(outa), .sel(adda));  // open: en
  Demultiplexer #(.select(2)) demultiplexer_1 (
    .out0(en0), .out1(en1), .out2(en2), .out3(en3), .in(en), .sel(adda));  // open: en
endmodule

module CPU (
  input  [1:0] in_1,
  input  [7:0] in_2,
  input  movecons,
  input  [1:0] in_4,
  input  in_5,
  input  [1:0] in_6
);

  wire clk;
  wire [7:0] multiplexer_1_out, outula, regs_1_outa, regs_1_outb;

  Clock clock_1 (.out(clk));
  Multiplexer #(.width(8)) multiplexer_1 (
    .in0(outula), .in1(in_2), .out(multiplexer_1_out), .sel(movecons));  // open: en
  // Probe on regs_1_outa
  REGS regs_1 (
    .adda(in_1), .addb(in_4), .\input (multiplexer_1_out), .clk(clk), .en(in_5), .outa(regs_1_outa),
    .outb(regs_1_outb));  // open: reset
  // Probe on regs_1_outb
  ULA ula_1 (.A(regs_1_outa), .B(regs_1_outb), .S(in_6), .out_4(outula));  // open: out_5
endmodule
